// Logisim project 4COM1042.circ-T02L1e02.circ as structural Verilog: 1 circuit, main circuit solution
module solution (
  input  [5:0] A,
  input  C_in,
  output C_out,
  output [5:0] R
);


  assign C_out = A[0];
  assign R = {C_in, A[5:1]};
endmodule
