// Logisim project 4COM1042.circ-T02L1e03.circ as structural Verilog: 2 circuits, main circuit solution
module solution (
  input  [5:0] A,
  input  C_in,
  input  [5:0] B,
  output [5:0] R,
  output C_out
);

  wire [5:0] and_1_out, and_2_out, xor_1_out;
  wire [5:1] or_1_out;

  // Probe on A
  // Probe on B
  assign xor_1_out = B ^ {or_1_out, C_in};  // XOR_Gate xor_1, 6 bits wide
  assign and_1_out = B & {or_1_out, C_in};  // AND_Gate and_1, 6 bits wide
  assign R = A ^ xor_1_out;  // XOR_Gate xor_2, 6 bits wide
  assign and_2_out = A & xor_1_out;  // AND_Gate and_2, 6 bits wide
  assign {C_out, or_1_out} = and_2_out | and_1_out;  // OR_Gate or_1, 6 bits wide
  // Probe on R
endmodule

module one_bit_adder (
  input  A,
  input  B,
  input  C_in,
  output SUM,
  output C_out
);

  wire and_1_out, and_2_out, and_3_out;

  and and_1 (and_1_out, A, B);
  and and_2 (and_2_out, C_in, B);
  and and_3 (and_3_out, A, C_in);
  xor xor_1 (SUM, A, B, C_in);
  or or_1 (C_out, and_1_out, and_2_out, and_3_out);
endmodule
