// Logisim project 4COM1042.circ-T02L1e05.circ as structural Verilog: 1 circuit, main circuit solution
module solution (
  input  [3:0] A,
  output [5:0] R
);


  assign R = {{3{A[3]}}, A[2:0]};
endmodule
