// Logisim project 4COM1042.circ-T02L1e06.circ as structural Verilog: 1 circuit, main circuit solution
module solution (
  input  [1:0] A,
  input  E,
  output R0,
  output R1,
  output R2,
  output R3
);

  wire and_1_out, and_2_out, and_3_out, and_4_out;

  and and_1 (and_1_out, ~E, ~A[1]);  // AND_Gate
  and and_2 (and_2_out, ~E, A[1]);  // AND_Gate
  and and_3 (and_3_out, E, ~A[1]);  // AND_Gate
  and and_4 (and_4_out, E, A[1]);
  and and_5 (R0, and_1_out, A[0]);
  and and_6 (R1, and_2_out, A[0]);
  and and_7 (R2, and_3_out, A[0]);
  and and_8 (R3, and_4_out, A[0]);
endmodule
