// Logisim project adders.circ as structural Verilog: 4 circuits, main circuit main
module main (
  input  carry_in,
  input  Input_a,
  input  Input_b,
  input  carry_in_2,
  input  [3:0] Input_A_2,
  input  [3:0] Input_B_2,
  input  carry_in_3,
  input  [7:0] Input_A_3,
  input  [7:0] Input_B_3,
  output sum,
  output carry_out,
  output [3:0] Sum_2,
  output carry_out_2,
  output [7:0] Sum_3,
  output carry_out_3
);

  // Probe on Input_A_2
  // Probe on Input_B_2
  // Probe on Input_A_3
  // Probe on Input_B_3
  _1_bit_adder u_1_bit_adder_1 (.A(carry_in), .B(Input_a), .C_in(Input_b), .Sum(sum), .C_out(carry_out));
  _4_bit_adder u_4_bit_adder_1 (
    .Carry_in(carry_in_2), .Input_A(Input_A_2), .Input_B(Input_B_2), .Sum(Sum_2), .Carry_out(carry_out_2));
  _8_bit_adder__2x4_bit u_8_bit_adder_2x4_bit_1 (
    .carry_in(carry_in_3), .Input_A(Input_A_3), .Input_B(Input_B_3), .Sum(Sum_3), .carry_out(carry_out_3));
  // Probe on Sum_2
  // Probe on Sum_3
endmodule

// ADD1
module _1_bit_adder (
  input  A,
  input  B,
  input  C_in,
  output Sum,
  output C_out
);

  wire and_1_out, and_2_out, xor_1_out;

  xor xor_1 (xor_1_out, B, C_in);
  and and_1 (and_1_out, B, C_in);
  xor xor_2 (Sum, A, xor_1_out);
  and and_2 (and_2_out, A, xor_1_out);
  or or_1 (C_out, and_2_out, and_1_out);
endmodule

// ADD4
module _4_bit_adder (
  input  Carry_in,
  input  [3:0] Input_A,
  input  [3:0] Input_B,
  output [3:0] Sum,
  output Carry_out
);

  wire n1_bit_adder_1_c_out, n1_bit_adder_2_c_out, n1_bit_adder_3_c_out;

  // Probe on Input_A
  // Probe on Input_B
  _1_bit_adder u_1_bit_adder_1 (
    .A(Input_A[0]), .B(Input_B[0]), .C_in(Carry_in), .Sum(Sum[0]), .C_out(n1_bit_adder_1_c_out));
  _1_bit_adder u_1_bit_adder_2 (
    .A(Input_A[1]), .B(Input_B[1]), .C_in(n1_bit_adder_1_c_out), .Sum(Sum[1]), .C_out(n1_bit_adder_2_c_out));
  _1_bit_adder u_1_bit_adder_3 (
    .A(Input_A[2]), .B(Input_B[2]), .C_in(n1_bit_adder_2_c_out), .Sum(Sum[2]), .C_out(n1_bit_adder_3_c_out));
  _1_bit_adder u_1_bit_adder_4 (
    .A(Input_A[3]), .B(Input_B[3]), .C_in(n1_bit_adder_3_c_out), .Sum(Sum[3]), .C_out(Carry_out));
  // Probe on Sum
endmodule

// ADD8
module _8_bit_adder__2x4_bit (
  input  carry_in,
  input  [7:0] Input_A,
  input  [7:0] Input_B,
  output [7:0] Sum,
  output carry_out
);

  wire n4_bit_adder_1_carry_out;

  // Probe on Input_A
  // Probe on Input_B
  _4_bit_adder u_4_bit_adder_1 (
    .Carry_in(carry_in), .Input_A(Input_A[3:0]), .Input_B(Input_B[3:0]), .Sum(Sum[3:0]),
    .Carry_out(n4_bit_adder_1_carry_out));
  _4_bit_adder u_4_bit_adder_2 (
    .Carry_in(n4_bit_adder_1_carry_out), .Input_A(Input_A[7:4]), .Input_B(Input_B[7:4]), .Sum(Sum[7:4]),
    .Carry_out(carry_out));
  // Probe on Sum
endmodule
