// Logisim project 4COM1042.circ-T03L2e01.circ as structural Verilog: 1 circuit, main circuit solution
module solution (
  input  X1,
  input  X2,
  input  X3,
  input  X4,
  input  X5,
  input  X6,
  input  X7,
  output [2:0] N
);

  wire [2:0] and_1_out, and_2_out, and_3_out, and_4_out, and_5_out, and_6_out, and_7_out;

  and and_1 (and_1_out[0], ~X1, ~X2, ~X3, ~X4, ~X5, ~X6, ~X7);  // AND_Gate
  and and_2 (and_2_out[0], X1, X1, X1, X1, X1, X1, X1);
  and and_3 (and_3_out[0], X1, X1, X1, X1, X1, X1, X1);
  and and_4 (and_4_out[0], X1, X1, X1, X1, X1, X1, X1);
  and and_5 (and_5_out[0], X1, X1, X1, X1, X1, X1, X1);
  and and_6 (and_6_out[0], X1, X1, X1, X1, X1, X1, X1);
  and and_7 (and_7_out[0], X1, X1, X1, X1, X1, X1, X1);
  ExactlyOne xor_1[2:0] (
    .in0(and_1_out), .in1(and_2_out), .in2(and_3_out), .in3(and_4_out), .in4(and_5_out), .in5(and_6_out),
    .in6(and_7_out));  // open: out
  // Probe on N
  // Pins of 1 and 3 bits meet at and_3_out
  // Pins of 1 and 3 bits meet at and_1_out
  // Pins of 1 and 3 bits meet at and_2_out
  // Pins of 1 and 3 bits meet at and_4_out
  // Pins of 1 and 3 bits meet at and_5_out
  // Pins of 1 and 3 bits meet at and_6_out
  // Pins of 1 and 3 bits meet at and_7_out
endmodule
