// Logisim project 4COM1042.circ-T03L1e07.circ as structural Verilog: 4 circuits, main circuit solution
module solution (
  input  [7:0] U,
  input  [7:0] W,
  output R
);

  wire not_2_out;
  wire [7:0] n8_bit_adder_2_sum, n8_bit_incrementer_2_r, n8_bit_incrementer_3_r, n8_bit_incrementer_4_r,
       n8_bit_incrementer_5_r, n8_bit_incrementer_6_r, n8_bit_incrementer_7_r, not_1_out;

  _8_bit_incrementer u_8_bit_incrementer_1 ();  // open: X, R, Cout
  // Probe on U
  // Probe on W
  assign not_1_out = ~U;  // NOT_Gate not_1, 8 bits wide
  _8_bit_incrementer u_8_bit_incrementer_2 (.X(W), .R(n8_bit_incrementer_2_r));  // open: Cout
  _8_bit_MUX u_8_bit_mux_1 ();  // open: Input_0, sel, Input_1, Output
  _8_bit_incrementer u_8_bit_incrementer_3 (.X(not_1_out), .R(n8_bit_incrementer_3_r));  // open: Cout
  _8_bit_incrementer u_8_bit_incrementer_4 (.X(n8_bit_incrementer_2_r), .R(n8_bit_incrementer_4_r));  // open: Cout
  _8_bit_incrementer u_8_bit_incrementer_5 (.X(n8_bit_incrementer_4_r), .R(n8_bit_incrementer_5_r));  // open: Cout
  _8_bit_incrementer u_8_bit_incrementer_6 (.X(n8_bit_incrementer_5_r), .R(n8_bit_incrementer_6_r));  // open: Cout
  _8_bit_incrementer u_8_bit_incrementer_7 (.X(n8_bit_incrementer_6_r), .R(n8_bit_incrementer_7_r));  // open: Cout
  _8_bit_adder u_8_bit_adder_1 ();  // open: A, B, sum, C, C_in
  _8_bit_adder u_8_bit_adder_2 (
    .A(n8_bit_incrementer_3_r), .B(n8_bit_incrementer_7_r), .sum(n8_bit_adder_2_sum));  // open: C, C_in
  not not_2 (not_2_out, not_2_out);
  and and_1 (R, ~n8_bit_adder_2_sum[0], ~n8_bit_adder_2_sum[1], ~n8_bit_adder_2_sum[2], ~n8_bit_adder_2_sum[3], ~n8_bit_adder_2_sum[4], ~n8_bit_adder_2_sum[5], ~n8_bit_adder_2_sum[6], ~n8_bit_adder_2_sum[7]);  // AND_Gate
  // NOT_Gate not_3 is placed but not wired
  // OR_Gate or_1 is placed but not wired
  // OR_Gate or_2 is placed but not wired
  // AND_Gate and_2 is placed but not wired
  // AND_Gate and_3 is placed but not wired
  // XOR_Gate xor_1 is placed but not wired
  // XOR_Gate xor_2 is placed but not wired
  // XNOR_Gate xnor_1 is placed but not wired

  // Notes on the sheet:
  //   BOTH INPUTS use 2's comp
  //   signed decimal:
  //   signed decimal:
  //   split a bunch into 8 individual wires
  //   all the above are 8-bit devices
  //   You are only allowed to use Wiring and Gates libraries
  //   Chips you may use in addition to gates (Click and Ctrl/D duplicates):
  //   out = A if sel=0
  //   B if sel=1
  //   You may also use the following (and any other)  splitters facing any direction
  //   ATTENTION! DO NOT MOVE ANY PINS!
  //   Ignore overflow, unless instructed otherwise
  //   extract the sign bit (bit 7) from an 8-bit bunch
  //   extract the LSB  (bit 0) from an 8-bit bunch
  //   Gates: Click and Ctrl/D duplicates
endmodule

module _8_bit_incrementer (
  input  [7:0] X,
  output [7:0] R,
  output Cout
);

  wire [7:1] and_1_out;

  assign {Cout, and_1_out} = {and_1_out, 1'b1} & X;  // AND_Gate and_1, 8 bits wide
  assign R = X ^ {and_1_out, 1'b1};  // XOR_Gate xor_1, 8 bits wide
endmodule

module _8_bit_adder (
  input  C_in,
  input  [7:0] A,
  input  [7:0] B,
  output [7:0] sum,
  output C
);

  wire [6:0] or_1_out;
  wire [7:0] and_1_out, and_2_out, and_3_out;

  Pull_Resistor pull_resistor_1 (.node(C_in));
  assign and_1_out = A & B;  // AND_Gate and_1, 8 bits wide
  assign and_2_out = B & {or_1_out, C_in};  // AND_Gate and_2, 8 bits wide
  assign and_3_out = A & {or_1_out, C_in};  // AND_Gate and_3, 8 bits wide
  assign {C, or_1_out} = and_1_out | and_2_out | and_3_out;  // OR_Gate or_1, 8 bits wide
  assign sum = A ^ {or_1_out, C_in} ^ B;  // XOR_Gate xor_1, 8 bits wide
endmodule

module _8_bit_MUX (
  input  [7:0] Input_0,
  input  sel,
  input  [7:0] Input_1,
  output [7:0] Output
);

  wire [7:0] and_1_out, and_2_out;
  wire [7:7] not_1_out;

  not not_1 (not_1_out[7], sel);
  assign and_1_out = Input_0 & {8{not_1_out[7]}};  // AND_Gate and_1, 8 bits wide
  assign and_2_out = {8{sel}} & Input_1;  // AND_Gate and_2, 8 bits wide
  assign Output = and_1_out | and_2_out;  // OR_Gate or_1, 8 bits wide
endmodule
