// Logisim project 4COM1042.circ-T03L1e15.circ as structural Verilog: 4 circuits, main circuit solution
module solution (
  input  [7:0] U,
  input  [7:0] W,
  output [7:0] Z
);

  wire not_4_out;
  wire [7:0] n8_bit_adder_1_sum, n8_bit_adder_2_sum, n8_bit_adder_4_sum, n8_bit_adder_5_sum,
       n8_bit_adder_6_sum, n8_bit_incrementer_2_r, n8_bit_incrementer_3_r, n8_bit_incrementer_4_r, not_1_out,
       not_2_out, not_3_out;

  _8_bit_incrementer u_8_bit_incrementer_1 ();  // open: X, R, Cout
  // Probe on U
  // Probe on W
  assign not_1_out = ~W;  // NOT_Gate not_1, 8 bits wide
  _8_bit_MUX u_8_bit_mux_1 ();  // open: Input_0, sel, Input_1, Output
  assign not_2_out = ~U;  // NOT_Gate not_2, 8 bits wide
  _8_bit_incrementer u_8_bit_incrementer_2 (.X(not_1_out), .R(n8_bit_incrementer_2_r));  // open: Cout
  _8_bit_incrementer u_8_bit_incrementer_3 (.X(not_2_out), .R(n8_bit_incrementer_3_r));  // open: Cout
  _8_bit_adder u_8_bit_adder_1 (.A(U), .B(n8_bit_incrementer_2_r), .sum(n8_bit_adder_1_sum));  // open: C, C_in
  assign not_3_out = ~U;  // NOT_Gate not_3, 8 bits wide
  _8_bit_incrementer u_8_bit_incrementer_4 (.X(not_3_out), .R(n8_bit_incrementer_4_r));  // open: Cout
  _8_bit_adder u_8_bit_adder_2 (
    .A(n8_bit_adder_1_sum), .B(n8_bit_adder_1_sum), .sum(n8_bit_adder_2_sum));  // open: C, C_in
  _8_bit_adder u_8_bit_adder_3 ();  // open: A, B, sum, C, C_in
  _8_bit_adder u_8_bit_adder_4 (.A(W), .B(n8_bit_incrementer_4_r), .sum(n8_bit_adder_4_sum));  // open: C, C_in
  _8_bit_adder u_8_bit_adder_5 (.A(n8_bit_incrementer_3_r), .B(W), .sum(n8_bit_adder_5_sum));  // open: C, C_in
  // Probe on n8_bit_adder_5_sum
  // Probe on n8_bit_adder_6_sum
  _8_bit_adder u_8_bit_adder_6 (
    .A(n8_bit_adder_2_sum), .B(n8_bit_adder_2_sum), .sum(n8_bit_adder_6_sum));  // open: C, C_in
  not not_4 (not_4_out, not_4_out);
  _8_bit_MUX u_8_bit_mux_2 (
    .Input_0(n8_bit_adder_6_sum), .sel(n8_bit_adder_5_sum[7]), .Input_1(n8_bit_adder_4_sum), .Output(Z));
  // NOT_Gate not_5 is placed but not wired
  // Probe on Z
  // OR_Gate or_1 is placed but not wired
  // OR_Gate or_2 is placed but not wired
  // AND_Gate and_1 is placed but not wired
  // AND_Gate and_2 is placed but not wired
  // XOR_Gate xor_1 is placed but not wired
  // XOR_Gate xor_2 is placed but not wired
  // XNOR_Gate xnor_1 is placed but not wired

  // Notes on the sheet:
  //   signed decimal:
  //   signed decimal:
  //   split a bunch into 8 individual wires
  //   Both U and W are signed numbers in 2's complement
  //   all the above are 8-bit devices
  //   You are only allowed to use Wiring and Gates libraries
  //   Chips you may use in addition to gates (Click and Ctrl/D duplicates):
  //   out = A if sel=0
  //   B if sel=1
  //   You may also use the following (and any other)  splitters facing any direction
  //   ATTENTION! DO NOT MOVE ANY PINS!
  //   Ignore overflow, unless instructed otherwise
  //   extract the sign bit (bit 7) from an 8-bit bunch
  //   extract the LSB  (bit 0) from an 8-bit bunch
  //   Gates: Click and Ctrl/D duplicates
endmodule

module _8_bit_incrementer (
  input  [7:0] X,
  output [7:0] R,
  output Cout
);

  wire [7:1] and_1_out;

  assign {Cout, and_1_out} = {and_1_out, 1'b1} & X;  // AND_Gate and_1, 8 bits wide
  assign R = X ^ {and_1_out, 1'b1};  // XOR_Gate xor_1, 8 bits wide
endmodule

module _8_bit_adder (
  input  C_in,
  input  [7:0] A,
  input  [7:0] B,
  output [7:0] sum,
  output C
);

  wire [6:0] or_1_out;
  wire [7:0] and_1_out, and_2_out, and_3_out;

  Pull_Resistor pull_resistor_1 (.node(C_in));
  assign and_1_out = A & B;  // AND_Gate and_1, 8 bits wide
  assign and_2_out = B & {or_1_out, C_in};  // AND_Gate and_2, 8 bits wide
  assign and_3_out = A & {or_1_out, C_in};  // AND_Gate and_3, 8 bits wide
  assign {C, or_1_out} = and_1_out | and_2_out | and_3_out;  // OR_Gate or_1, 8 bits wide
  assign sum = A ^ {or_1_out, C_in} ^ B;  // XOR_Gate xor_1, 8 bits wide
endmodule

module _8_bit_MUX (
  input  [7:0] Input_0,
  input  sel,
  input  [7:0] Input_1,
  output [7:0] Output
);

  wire [7:0] and_1_out, and_2_out;
  wire [7:7] not_1_out;

  not not_1 (not_1_out[7], sel);
  assign and_1_out = Input_0 & {8{not_1_out[7]}};  // AND_Gate and_1, 8 bits wide
  assign and_2_out = {8{sel}} & Input_1;  // AND_Gate and_2, 8 bits wide
  assign Output = and_1_out | and_2_out;  // OR_Gate or_1, 8 bits wide
endmodule
